# Fritzing sketch CPE301L_Schematic (saved by Fritzing 0.9.10b)
breadboards: 1

parts:
  U1 = LCD-16X2 [package=lcd-16x2]  # not connected
  M1 = Stepper Motor - Unipolar  # not connected
  Part2 = Real Time Clock Module - DS1307 RTC Breakout Board  # not connected
  IC1 = DS1307 [package=THT]  # not connected
  U2 = DS1307 [package=so08]  # not connected
  Part1 = Arduino Mega 2560 (Rev3)
  DHT11 = Humidity and Temperature Sensor DHT11
  BLUE_LED = LEDs [package=led10mm]
  RED_LED = LEDs [package=led10mm]
  GREEN_LED = LEDs [package=led10mm]
  YELLOW_LED = LEDs [package=led10mm]
  R1 = Resistor [tolerance=±5% resistance=330 package="0805 [SMD]"]
  R2 = Resistor [tolerance=±5% resistance=330 package="0805 [SMD]"]
  R3 = Resistor [tolerance=±5% resistance=330 package="0805 [SMD]"]
  R4 = Resistor [tolerance=±5% resistance=330 package="0805 [SMD]"]

nets:
  N1: Part1.GND, DHT11.GND_1, BLUE_LED.C, RED_LED.C, GREEN_LED.C, YELLOW_LED.C
  5V: Part1.5V, DHT11.Vcc
  N2: BLUE_LED.A, R1.Pin_1
  N3: RED_LED.A, R2.Pin_1
  N4: GREEN_LED.A, R3.Pin_1
  N5: YELLOW_LED.A, R4.Pin_1

custom parts:
  Humidity and Temperature Sensor DHT11: Digital relative humidity & temperature sensor DHT11
